# Fritzing sketch ndor (saved by Fritzing 0.9.3b)
breadboards: 1

parts:
  Part1 = Arduino Uno (Rev3) - ICSP
  J2 = Piezo Speaker
  hc-sr1 = hc-sr04
  LED1 = LED - 3mm [color="Red (633nm)" package="3 mm [THT]"]
  J3 = Basic Servo

nets:
  N1: Part1.ICSP_MISO, Part1.D12/MISO, LED1.cathode
  GND: Part1.GND, J2.pin1, hc-sr1.GND, LED1.anode, J3.gnd, J3.pulse
  N2: Part1.D8, hc-sr1.Echo
  N3: Part1.D9_PWM, hc-sr1.Trig
  N4: Part1.D7, J2.pin2
  VCC: Part1.5V, hc-sr1.VCC, J3.vcc
